// Logisim project digital clock.circ as structural Verilog: 7 circuits, main circuit main
module main (
  input  no_power,
  input  power
);

  wire clock_out, engine_1_a_1_hour, engine_1_a_1_minute, engine_1_a_1_second, engine_1_a_10_hour,
       engine_1_a_10_minute, engine_1_a_10_second, engine_1_b_1_hour, engine_1_b_1_minute,
       engine_1_b_1_second, engine_1_b_10_hour, engine_1_b_10_minute, engine_1_b_10_second,
       engine_1_c_1_hour, engine_1_c_1_minute, engine_1_c_1_second, engine_1_c_10_hour, engine_1_c_10_minute,
       engine_1_c_10_second, engine_1_d_1_hour, engine_1_d_1_minute, engine_1_d_1_second, engine_1_d_10_hour,
       engine_1_d_10_minute, engine_1_d_10_second, engine_1_e_1_hour, engine_1_e_1_minute,
       engine_1_e_1_second, engine_1_e_10_hour, engine_1_e_10_minute, engine_1_e_10_second,
       engine_1_f_1_hour, engine_1_f_1_minute, engine_1_f_1_second, engine_1_f_10_hour, engine_1_f_10_minute,
       engine_1_f_10_second, engine_1_g_1_hour, engine_1_g_1_minute, engine_1_g_1_second, engine_1_g_10_hour,
       engine_1_g_10_minute, engine_1_g_10_second;

  Clock clock (.out(clock_out));
  Engine engine_1 (
    .no_power(no_power), .power(power), .clock(clock_out), .a_10_hour(engine_1_a_10_hour),
    .b_10_hour(engine_1_b_10_hour), .c_10_hour(engine_1_c_10_hour), .d_10_hour(engine_1_d_10_hour),
    .e_10_hour(engine_1_e_10_hour), .f_10_hour(engine_1_f_10_hour), .g_10_hour(engine_1_g_10_hour),
    .a_1_hour(engine_1_a_1_hour), .b_1_hour(engine_1_b_1_hour), .c_1_hour(engine_1_c_1_hour),
    .d_1_hour(engine_1_d_1_hour), .e_1_hour(engine_1_e_1_hour), .f_1_hour(engine_1_f_1_hour),
    .g_1_hour(engine_1_g_1_hour), .a_10_minute(engine_1_a_10_minute), .b_10_minute(engine_1_b_10_minute),
    .c_10_minute(engine_1_c_10_minute), .d_10_minute(engine_1_d_10_minute),
    .e_10_minute(engine_1_e_10_minute), .f_10_minute(engine_1_f_10_minute),
    .g_10_minute(engine_1_g_10_minute), .a_1_minute(engine_1_a_1_minute), .b_1_minute(engine_1_b_1_minute),
    .c_1_minute(engine_1_c_1_minute), .d_1_minute(engine_1_d_1_minute), .e_1_minute(engine_1_e_1_minute),
    .f_1_minute(engine_1_f_1_minute), .g_1_minute(engine_1_g_1_minute), .a_10_second(engine_1_a_10_second),
    .b_10_second(engine_1_b_10_second), .c_10_second(engine_1_c_10_second),
    .d_10_second(engine_1_d_10_second), .e_10_second(engine_1_e_10_second),
    .f_10_second(engine_1_f_10_second), .g_10_second(engine_1_g_10_second), .a_1_second(engine_1_a_1_second),
    .b_1_second(engine_1_b_1_second), .c_1_second(engine_1_c_1_second), .d_1_second(engine_1_d_1_second),
    .e_1_second(engine_1_e_1_second), .f_1_second(engine_1_f_1_second), .g_1_second(engine_1_g_1_second));
  _7_Segment_Display u_7_segment_display_1 (
    .g(engine_1_g_1_hour), .f(engine_1_f_1_hour), .a(engine_1_a_1_hour), .b(engine_1_b_1_hour),
    .e(engine_1_e_1_hour), .d(engine_1_d_1_hour), .c(engine_1_c_1_hour));  // open: dp
  _7_Segment_Display u_7_segment_display_2 (
    .g(engine_1_g_10_hour), .f(engine_1_f_10_hour), .a(engine_1_a_10_hour), .b(engine_1_b_10_hour),
    .e(engine_1_e_10_hour), .d(engine_1_d_10_hour), .c(engine_1_c_10_hour));  // open: dp
  _7_Segment_Display u_7_segment_display_3 (
    .g(engine_1_g_10_minute), .f(engine_1_f_10_minute), .a(engine_1_a_10_minute), .b(engine_1_b_10_minute),
    .e(engine_1_e_10_minute), .d(engine_1_d_10_minute), .c(engine_1_c_10_minute));  // open: dp
  _7_Segment_Display u_7_segment_display_4 (
    .g(engine_1_g_1_minute), .f(engine_1_f_1_minute), .a(engine_1_a_1_minute), .b(engine_1_b_1_minute),
    .e(engine_1_e_1_minute), .d(engine_1_d_1_minute), .c(engine_1_c_1_minute));  // open: dp
  _7_Segment_Display u_7_segment_display_5 (
    .g(engine_1_g_10_second), .f(engine_1_f_10_second), .a(engine_1_a_10_second), .b(engine_1_b_10_second),
    .e(engine_1_e_10_second), .d(engine_1_d_10_second), .c(engine_1_c_10_second));  // open: dp
  _7_Segment_Display u_7_segment_display_6 (
    .g(engine_1_g_1_second), .f(engine_1_f_1_second), .a(engine_1_a_1_second), .b(engine_1_b_1_second),
    .e(engine_1_e_1_second), .d(engine_1_d_1_second), .c(engine_1_c_1_second));  // open: dp

  // Notes on the sheet:
  //   By Seonung Moon
  //   2024-05-27
  //   Turn on the power and set the clock to 1Hz
endmodule

module _7_segment_Decoder (
  input  w,
  input  x,
  input  y,
  input  z,
  output a,
  output b,
  output c,
  output d,
  output e,
  output f,
  output g
);

  wire not_1_out, not_2_out, not_3_out, not_4_out, not_5_out, not_6_out, not_7_out, not_8_out, not_9_out,
       not_10_out, not_11_out, not_12_out, not_13_out, not_14_out, not_15_out, not_16_out, not_17_out,
       not_18_out, not_19_out, not_20_out, not_21_out, x_prime_y_2_out, x_prime_y_out, x_prime_z_prime_2_out,
       x_prime_z_prime_3_out, x_prime_z_prime_out, xy_prime_2_out, xy_prime_out, xy_prime_z_out, xz_out,
       xz_prime_2_out, xz_prime_out, y_prime_z_prime_2_out, y_prime_z_prime_out, yz_out, yz_prime_2_out,
       yz_prime_out;

  not not_1 (not_1_out, x);
  not not_2 (not_2_out, z);
  not not_3 (not_3_out, x);
  not not_4 (not_4_out, y);
  not not_5 (not_5_out, z);
  not not_6 (not_6_out, y);
  not not_7 (not_7_out, x);
  not not_8 (not_8_out, z);
  not not_9 (not_9_out, x);
  not not_10 (not_10_out, z);
  not not_11 (not_11_out, y);
  not not_12 (not_12_out, x);
  not not_13 (not_13_out, z);
  not not_14 (not_14_out, z);
  not not_15 (not_15_out, y);
  not not_16 (not_16_out, z);
  not not_17 (not_17_out, y);
  not not_18 (not_18_out, z);
  not not_19 (not_19_out, x);
  not not_20 (not_20_out, y);
  not not_21 (not_21_out, z);
  and x_prime_z_prime (x_prime_z_prime_out, not_1_out, not_2_out);
  and xz (xz_out, x, z);
  and yz (yz_out, y, z);
  and y_prime_z_prime (y_prime_z_prime_out, not_4_out, not_5_out);
  and x_prime_z_prime_2 (x_prime_z_prime_2_out, not_7_out, not_8_out);
  and x_prime_y (x_prime_y_out, not_9_out, y);
  and yz_prime (yz_prime_out, y, not_10_out);
  and xy_prime_z (xy_prime_z_out, x, not_11_out, z);
  and x_prime_z_prime_3 (x_prime_z_prime_3_out, not_12_out, not_13_out);
  and yz_prime_2 (yz_prime_2_out, y, not_14_out);
  and y_prime_z_prime_2 (y_prime_z_prime_2_out, not_15_out, not_16_out);
  and xy_prime (xy_prime_out, x, not_17_out);
  and xz_prime (xz_prime_out, x, not_18_out);
  and x_prime_y_2 (x_prime_y_2_out, not_19_out, y);
  and xy_prime_2 (xy_prime_2_out, x, not_20_out);
  and xz_prime_2 (xz_prime_2_out, x, not_21_out);
  or or_1 (a, x_prime_z_prime_out, y, xz_out, w);
  or or_2 (b, yz_out, not_3_out, y_prime_z_prime_out);
  or xy_prime_z_2 (c, x, not_6_out, z);
  or or_3 (d, x_prime_z_prime_2_out, x_prime_y_out, yz_prime_out, xy_prime_z_out, w);
  or or_4 (e, x_prime_z_prime_3_out, yz_prime_2_out);
  or or_5 (f, y_prime_z_prime_2_out, xy_prime_out, xz_prime_out, w);
  or or_6 (g, x_prime_y_2_out, xy_prime_2_out, xz_prime_2_out, w);
endmodule

module _10_Counter (
  input  power,
  input  clock,
  input  signal,
  output w,
  output x,
  output y,
  output z
);

  wire and_1_out, and_2_out, and_3_out, and_4_out;

  and and_1 (and_1_out, clock, signal);
  J_K_Flip_Flop j_k_ff_1 (.J(power), .clk(and_1_out), .K(power), .Q(z), .reset(and_4_out));  // open: Qn, preset, en
  J_K_Flip_Flop j_k_ff_2 (.J(z), .clk(and_1_out), .K(z), .Q(y), .reset(and_4_out));  // open: Qn, preset, en
  and and_2 (and_2_out, z, y);
  J_K_Flip_Flop j_k_ff_3 (
    .J(and_2_out), .clk(and_1_out), .K(and_2_out), .Q(x), .reset(and_4_out));  // open: Qn, preset, en
  and and_3 (and_3_out, x, and_2_out);
  J_K_Flip_Flop j_k_ff_4 (
    .J(and_3_out), .clk(and_1_out), .K(and_3_out), .Q(w), .reset(and_4_out));  // open: Qn, preset, en
  and and_4 (and_4_out, y, w);
endmodule

module _6_Counter (
  input  power,
  input  clock,
  input  signal,
  output w,
  output x,
  output y,
  output z
);

  wire and_1_out, and_2_out, and_3_out, and_4_out;

  and and_1 (and_1_out, clock, signal);
  J_K_Flip_Flop j_k_ff_1 (.J(power), .clk(and_1_out), .K(power), .Q(z), .reset(and_4_out));  // open: Qn, preset, en
  J_K_Flip_Flop j_k_ff_2 (.J(z), .clk(and_1_out), .K(z), .Q(y), .reset(and_4_out));  // open: Qn, preset, en
  and and_2 (and_2_out, z, y);
  J_K_Flip_Flop j_k_ff_3 (
    .J(and_2_out), .clk(and_1_out), .K(and_2_out), .Q(x), .reset(and_4_out));  // open: Qn, preset, en
  and and_3 (and_3_out, x, and_2_out);
  J_K_Flip_Flop j_k_ff_4 (
    .J(and_3_out), .clk(and_1_out), .K(and_3_out), .Q(w), .reset(and_4_out));  // open: Qn, preset, en
  and and_4 (and_4_out, y, x);
endmodule

module _3_Counter (
  input  power,
  input  clock,
  input  signal,
  output y,
  output z
);

  wire and_1_out, and_2_out;

  and and_1 (and_1_out, clock, signal);
  J_K_Flip_Flop j_k_ff_1 (.J(power), .clk(and_1_out), .K(power), .Q(z), .reset(and_2_out));  // open: Qn, preset, en
  J_K_Flip_Flop j_k_ff_2 (.J(z), .clk(and_1_out), .K(z), .Q(y), .reset(and_2_out));  // open: Qn, preset, en
  and and_2 (and_2_out, y, z);
endmodule

module _10_Counter_reset (
  input  power,
  input  clock,
  input  signal,
  input  reset,
  output w,
  output x,
  output y,
  output z
);

  wire and_1_out, and_2_out, and_3_out, and_4_out, or_1_out;

  and and_1 (and_1_out, clock, signal);
  J_K_Flip_Flop j_k_ff_1 (.J(power), .clk(and_1_out), .K(power), .Q(z), .reset(or_1_out));  // open: Qn, preset, en
  J_K_Flip_Flop j_k_ff_2 (.J(z), .clk(and_1_out), .K(z), .Q(y), .reset(or_1_out));  // open: Qn, preset, en
  and and_2 (and_2_out, z, y);
  J_K_Flip_Flop j_k_ff_3 (
    .J(and_2_out), .clk(and_1_out), .K(and_2_out), .Q(x), .reset(or_1_out));  // open: Qn, preset, en
  and and_3 (and_3_out, x, and_2_out);
  J_K_Flip_Flop j_k_ff_4 (
    .J(and_3_out), .clk(and_1_out), .K(and_3_out), .Q(w), .reset(or_1_out));  // open: Qn, preset, en
  or or_1 (or_1_out, and_4_out, reset);
  and and_4 (and_4_out, y, w);
endmodule

module Engine (
  input  no_power,
  input  power,
  input  clock,
  output a_10_hour,
  output b_10_hour,
  output c_10_hour,
  output d_10_hour,
  output e_10_hour,
  output f_10_hour,
  output g_10_hour,
  output a_1_hour,
  output b_1_hour,
  output c_1_hour,
  output d_1_hour,
  output e_1_hour,
  output f_1_hour,
  output g_1_hour,
  output a_10_minute,
  output b_10_minute,
  output c_10_minute,
  output d_10_minute,
  output e_10_minute,
  output f_10_minute,
  output g_10_minute,
  output a_1_minute,
  output b_1_minute,
  output c_1_minute,
  output d_1_minute,
  output e_1_minute,
  output f_1_minute,
  output g_1_minute,
  output a_10_second,
  output b_10_second,
  output c_10_second,
  output d_10_second,
  output e_10_second,
  output f_10_second,
  output g_10_second,
  output a_1_second,
  output b_1_second,
  output c_1_second,
  output d_1_second,
  output e_1_second,
  output f_1_second,
  output g_1_second
);

  wire _6_2_out, _6_out, _10_2_out, _10_3_out, _10_out, _24_out, n3_counter_1_y, n3_counter_1_z,
       n6_counter_1_w, n6_counter_1_x, n6_counter_1_y, n6_counter_1_z, n6_counter_2_w, n6_counter_2_x,
       n6_counter_2_y, n6_counter_2_z, n10_counter_1_w, n10_counter_1_x, n10_counter_1_y, n10_counter_1_z,
       n10_counter_2_w, n10_counter_2_x, n10_counter_2_y, n10_counter_2_z, n10_counter_reset_1_w,
       n10_counter_reset_1_x, n10_counter_reset_1_y, n10_counter_reset_1_z, or_1_out;

  or or_1 (or_1_out, _24_out, _10_out);
  _3_Counter u_3_counter_1 (.power(power), .clock(clock), .signal(or_1_out), .y(n3_counter_1_y), .z(n3_counter_1_z));
  and _24 (_24_out, n3_counter_1_y, n10_counter_reset_1_x);
  and _10 (_10_out, n10_counter_reset_1_y, n10_counter_reset_1_w);
  _10_Counter_reset u_10_counter_reset_1 (
    .power(power), .clock(clock), .signal(_6_out), .reset(_24_out), .w(n10_counter_reset_1_w),
    .x(n10_counter_reset_1_x), .y(n10_counter_reset_1_y), .z(n10_counter_reset_1_z));
  and _6 (_6_out, n6_counter_1_y, n6_counter_1_x);
  _6_Counter u_6_counter_1 (
    .power(power), .clock(clock), .signal(_10_2_out), .w(n6_counter_1_w), .x(n6_counter_1_x),
    .y(n6_counter_1_y), .z(n6_counter_1_z));
  and _10_2 (_10_2_out, n10_counter_1_y, n10_counter_1_w);
  _10_Counter u_10_counter_1 (
    .power(power), .clock(clock), .signal(_6_2_out), .w(n10_counter_1_w), .x(n10_counter_1_x),
    .y(n10_counter_1_y), .z(n10_counter_1_z));
  and _6_2 (_6_2_out, n6_counter_2_y, n6_counter_2_x);
  _6_Counter u_6_counter_2 (
    .power(power), .clock(clock), .signal(_10_3_out), .w(n6_counter_2_w), .x(n6_counter_2_x),
    .y(n6_counter_2_y), .z(n6_counter_2_z));
  and _10_3 (_10_3_out, n10_counter_2_y, n10_counter_2_w);
  _10_Counter u_10_counter_2 (
    .power(power), .clock(clock), .signal(power), .w(n10_counter_2_w), .x(n10_counter_2_x),
    .y(n10_counter_2_y), .z(n10_counter_2_z));
  _7_segment_Decoder hour__tens_place (
    .w(no_power), .x(no_power), .y(n3_counter_1_y), .z(n3_counter_1_z), .a(a_10_hour), .b(b_10_hour),
    .c(c_10_hour), .d(d_10_hour), .e(e_10_hour), .f(f_10_hour), .g(g_10_hour));
  _7_segment_Decoder hour__ones_place (
    .w(n10_counter_reset_1_w), .x(n10_counter_reset_1_x), .y(n10_counter_reset_1_y),
    .z(n10_counter_reset_1_z), .a(a_1_hour), .b(b_1_hour), .c(c_1_hour), .d(d_1_hour), .e(e_1_hour),
    .f(f_1_hour), .g(g_1_hour));
  _7_segment_Decoder minute__tens_place (
    .w(n6_counter_1_w), .x(n6_counter_1_x), .y(n6_counter_1_y), .z(n6_counter_1_z), .a(a_10_minute),
    .b(b_10_minute), .c(c_10_minute), .d(d_10_minute), .e(e_10_minute), .f(f_10_minute), .g(g_10_minute));
  _7_segment_Decoder minute__ones_place (
    .w(n10_counter_1_w), .x(n10_counter_1_x), .y(n10_counter_1_y), .z(n10_counter_1_z), .a(a_1_minute),
    .b(b_1_minute), .c(c_1_minute), .d(d_1_minute), .e(e_1_minute), .f(f_1_minute), .g(g_1_minute));
  _7_segment_Decoder second__tens_place (
    .w(n6_counter_2_w), .x(n6_counter_2_x), .y(n6_counter_2_y), .z(n6_counter_2_z), .a(a_10_second),
    .b(b_10_second), .c(c_10_second), .d(d_10_second), .e(e_10_second), .f(f_10_second), .g(g_10_second));
  _7_segment_Decoder second__ones_place (
    .w(n10_counter_2_w), .x(n10_counter_2_x), .y(n10_counter_2_y), .z(n10_counter_2_z), .a(a_1_second),
    .b(b_1_second), .c(c_1_second), .d(d_1_second), .e(e_1_second), .f(f_1_second), .g(g_1_second));
endmodule
